# Fritzing sketch schematic (saved by Fritzing 0.9.5d)

parts:
  Part1 = Adafruit Feather M0 Basic Proto [part_number="Adafruit #2772"]
  Part2 = Adafruit AD8495 [part_number="Adafruit #1778"]
  Part3 = Adafruit Quad AlphaNumeric Featherwing - White [part_number="Adafruit #3127"]

nets:
  N1: Part1.A5, Part2.OUT
  GND: Part1.GND, Part2.GND, Part3.GND
  +3V3: Part1.+3V3, Part2.VIN
  N2: Part1.SCL, Part3.SCL
  N3: Part1.SDA, Part3.SDA

custom parts:
  Adafruit Feather M0 Basic Proto: At the Feather M0's heart is an ATSAMD21G18 ARM Cortex M0 processor, clocked at 48 MHz and at 3.3V logic, the same one used in the new Arduino Zero. This chip has a whopping 256K of FLASH (8x more than the Atmega328 or 32u4) and 32K of RAM (16x as much)! This chip comes with built in USB so it has USB-to-Serial program & debug capability built in with no need for an FTDI-like chip. To make it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
  Adafruit AD8495: Thermocouples are very sensitive, requiring a good amplifier with a cold-compensation reference. We have a couple digital thermocouple amplifiers in the shop already from Maxim. Now we're happy to introduce an excellent analog-output amplifier. This is a very simple sensor to use, and if your microcontroller has analog input capability, you'll be ready to go really fast! The AD8495 K-type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
  Adafruit Quad AlphaNumeric Featherwing - White: This is the White Adafruit 0.54" Dual Alphanumeric Display w/ FeatherWing Combo Pack! We also have these combo packs in Green, Red, Yellow-Green, Blue, and Yellow. This is a nice, bright alphanumeric display that shows letters and numbers in a beautiful hue. It's super bright and designed for viewing from distances up to 23 feet (7 meters) away. Each of the digit sets have 14 segments on a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
